// Logisim project cpu_risc_v.circ as structural Verilog
module interger_register_file (
  input  Clock,
  input  EnableX0,
  input  EnableWrite,
  input  [3:0] ReadRegisterY,
  input  EnableRead,
  input  [3:0] ReadRegisterX,
  input  [3:0] SetRegister,
  input  [31:0] Data,
  output [31:0] OutputY,
  output [31:0] OutputX
);

  wire and_1_out, decoder_1_out0, decoder_1_out1, decoder_1_out2, decoder_1_out3, decoder_1_out4,
       decoder_1_out5, decoder_1_out6, decoder_1_out7, decoder_1_out8, decoder_1_out9, decoder_1_out10,
       decoder_1_out11, decoder_1_out12, decoder_1_out13, decoder_1_out14, decoder_1_out15, ER0_out, ER1_out,
       ER2_out, ER3_out, ER4_out, ER5_out, ER6_out, ER7_out, ER8_out, ER9_out, ER10_out, ER11_out, ER12_out,
       ER13_out, ER14_out, ER15_out;
  wire [31:0] demultiplexer_1_out0, demultiplexer_1_out1, demultiplexer_1_out2, demultiplexer_1_out3,
       demultiplexer_1_out4, demultiplexer_1_out5, demultiplexer_1_out6, demultiplexer_1_out7,
       demultiplexer_1_out8, demultiplexer_1_out9, demultiplexer_1_out10, demultiplexer_1_out11,
       demultiplexer_1_out12, demultiplexer_1_out13, demultiplexer_1_out14, demultiplexer_1_out15,
       register_1_q, register_2_q, register_3_q, register_4_q, register_5_q, register_6_q, register_7_q,
       register_8_q, register_9_q, register_10_q, register_11_q, register_12_q, register_13_q, register_14_q,
       register_15_q, register_16_q;

  Decoder #(.enable("false"), .select(4)) decoder_1 (
    .out0(decoder_1_out0), .out1(decoder_1_out1), .out2(decoder_1_out2), .out3(decoder_1_out3),
    .out4(decoder_1_out4), .out5(decoder_1_out5), .out6(decoder_1_out6), .out7(decoder_1_out7),
    .out8(decoder_1_out8), .out9(decoder_1_out9), .out10(decoder_1_out10), .out11(decoder_1_out11),
    .out12(decoder_1_out12), .out13(decoder_1_out13), .out14(decoder_1_out14), .out15(decoder_1_out15),
    .sel(SetRegister));
  and ER0 (ER0_out, EnableWrite, decoder_1_out0);
  and ER1 (ER1_out, EnableWrite, decoder_1_out1);
  and ER2 (ER2_out, EnableWrite, decoder_1_out2);
  and ER3 (ER3_out, EnableWrite, decoder_1_out3);
  and ER4 (ER4_out, EnableWrite, decoder_1_out4);
  and ER5 (ER5_out, EnableWrite, decoder_1_out5);
  and ER6 (ER6_out, EnableWrite, decoder_1_out6);
  and ER7 (ER7_out, EnableWrite, decoder_1_out7);
  and ER8 (ER8_out, EnableWrite, decoder_1_out8);
  and ER9 (ER9_out, EnableWrite, decoder_1_out9);
  and ER10 (ER10_out, EnableWrite, decoder_1_out10);
  and ER11 (ER11_out, EnableWrite, decoder_1_out11);
  and ER12 (ER12_out, EnableWrite, decoder_1_out12);
  and ER13 (ER13_out, EnableWrite, decoder_1_out13);
  and ER14 (ER14_out, EnableWrite, decoder_1_out14);
  and ER15 (ER15_out, EnableWrite, decoder_1_out15);
  and and_1 (and_1_out, EnableX0, ER0_out);
  Register #(.width(32)) register_1 (
    .D(demultiplexer_1_out0), .en(and_1_out), .Q(register_1_q), .clk(Clock));  // open: clr
  Register #(.width(32)) register_2 (
    .D(demultiplexer_1_out1), .en(ER1_out), .Q(register_2_q), .clk(Clock));  // open: clr
  Register #(.width(32)) register_3 (
    .D(demultiplexer_1_out2), .en(ER2_out), .Q(register_3_q), .clk(Clock));  // open: clr
  Register #(.width(32)) register_4 (
    .D(demultiplexer_1_out3), .en(ER3_out), .Q(register_4_q), .clk(Clock));  // open: clr
  Register #(.width(32)) register_5 (
    .D(demultiplexer_1_out4), .en(ER4_out), .Q(register_5_q), .clk(Clock));  // open: clr
  Register #(.width(32)) register_6 (
    .D(demultiplexer_1_out5), .en(ER5_out), .Q(register_6_q), .clk(Clock));  // open: clr
  Register #(.width(32)) register_7 (
    .D(demultiplexer_1_out6), .en(ER6_out), .Q(register_7_q), .clk(Clock));  // open: clr
  Register #(.width(32)) register_8 (
    .D(demultiplexer_1_out7), .en(ER7_out), .Q(register_8_q), .clk(Clock));  // open: clr
  Demultiplexer #(.select(4), .width(32)) demultiplexer_1 (
    .out0(demultiplexer_1_out0), .out1(demultiplexer_1_out1), .out2(demultiplexer_1_out2),
    .out3(demultiplexer_1_out3), .out4(demultiplexer_1_out4), .out5(demultiplexer_1_out5),
    .out6(demultiplexer_1_out6), .out7(demultiplexer_1_out7), .out8(demultiplexer_1_out8),
    .out9(demultiplexer_1_out9), .out10(demultiplexer_1_out10), .out11(demultiplexer_1_out11),
    .out12(demultiplexer_1_out12), .out13(demultiplexer_1_out13), .out14(demultiplexer_1_out14),
    .out15(demultiplexer_1_out15), .in(Data), .sel(SetRegister));
  Register #(.width(32)) register_9 (
    .D(demultiplexer_1_out8), .en(ER8_out), .Q(register_9_q), .clk(Clock));  // open: clr
  Register #(.width(32)) register_10 (
    .D(demultiplexer_1_out9), .en(ER9_out), .Q(register_10_q), .clk(Clock));  // open: clr
  Register #(.width(32)) register_11 (
    .D(demultiplexer_1_out10), .en(ER10_out), .Q(register_11_q), .clk(Clock));  // open: clr
  Register #(.width(32)) register_12 (
    .D(demultiplexer_1_out11), .en(ER11_out), .Q(register_12_q), .clk(Clock));  // open: clr
  Register #(.width(32)) register_13 (
    .D(demultiplexer_1_out12), .en(ER12_out), .Q(register_13_q), .clk(Clock));  // open: clr
  Register #(.width(32)) register_14 (
    .D(demultiplexer_1_out13), .en(ER13_out), .Q(register_14_q), .clk(Clock));  // open: clr
  Register #(.width(32)) register_15 (
    .D(demultiplexer_1_out14), .en(ER14_out), .Q(register_15_q), .clk(Clock));  // open: clr
  Register #(.width(32)) register_16 (
    .D(demultiplexer_1_out15), .en(ER15_out), .Q(register_16_q), .clk(Clock));  // open: clr
  Multiplexer #(.enable("true"), .select(4), .width(32)) multiplexer_1 (
    .in0(register_1_q), .in1(register_2_q), .in2(register_3_q), .in3(register_4_q), .in4(register_5_q),
    .in5(register_6_q), .in6(register_7_q), .in7(register_8_q), .in8(register_9_q), .in9(register_10_q),
    .in10(register_11_q), .in11(register_12_q), .in12(register_13_q), .in13(register_14_q),
    .in14(register_15_q), .in15(register_16_q), .out(OutputY), .sel(ReadRegisterY), .en(EnableRead));
  Multiplexer #(.enable("true"), .select(4), .width(32)) multiplexer_2 (
    .in0(register_1_q), .in1(register_2_q), .in2(register_3_q), .in3(register_4_q), .in4(register_5_q),
    .in5(register_6_q), .in6(register_7_q), .in7(register_8_q), .in8(register_9_q), .in9(register_10_q),
    .in10(register_11_q), .in11(register_12_q), .in12(register_13_q), .in13(register_14_q),
    .in14(register_15_q), .in15(register_16_q), .out(OutputX), .sel(ReadRegisterX), .en(EnableRead));
endmodule

module vector_register_file (
  input  [31:0] inputA0,
  input  [31:0] inputA1,
  input  [31:0] inputA2,
  input  Clock,
  input  EnableWrite1,
  input  [3:0] WriteToResgisterX,
  input  [3:0] ClearRegisterX,
  input  [3:0] ClearRegisterY,
  input  ClearEnableX,
  input  ClearEnableY,
  input  [3:0] RegisterToReadX,
  input  [3:0] RegisterToReadY,
  output [31:0] X0,
  output [31:0] X1,
  output [31:0] X2,
  output [31:0] Y0,
  output [31:0] Y2,
  output [31:0] Y3
);

  wire ReadEnableController_output0, ReadEnableController_output1, ReadEnableController_output2,
       ReadEnableController_output3, ReadEnableController_output4, ReadEnableController_output5,
       ReadEnableController_output6, ReadEnableController_output7, ReadEnableController_output8,
       ReadEnableController_output9, ReadEnableController_output10, ReadEnableController_output11,
       ReadEnableController_output12, ReadEnableController_output13, ReadEnableController_output14,
       ReadEnableController_output15, WriteEnableController_output0, WriteEnableController_output1,
       WriteEnableController_output2, WriteEnableController_output3, WriteEnableController_output4,
       WriteEnableController_output5, WriteEnableController_output6, WriteEnableController_output7,
       WriteEnableController_output8, WriteEnableController_output9, WriteEnableController_output10,
       WriteEnableController_output11, WriteEnableController_output12, WriteEnableController_output13,
       WriteEnableController_output14, WriteEnableController_output15;
  wire [31:0] V0_output_0, V0_output_1, V0_output_2, V1_output_0, V1_output_1, V1_output_2, V2_output_0,
       V2_output_1, V2_output_2, V3_output_0, V3_output_1, V3_output_2, V4_output_0, V4_output_1,
       V4_output_2, V5_output_0, V5_output_1, V5_output_2, V6_output_0, V6_output_1, V6_output_2,
       V7_output_0, V7_output_1, V7_output_2, V8_output_0, V8_output_1, V8_output_2, V9_output_0,
       V9_output_1, V9_output_2, V10_output_0, V10_output_1, V10_output_2, V11_output_0, V11_output_1,
       V11_output_2, V12_output_0, V12_output_1, V12_output_2, V13_output_0, V13_output_1, V13_output_2,
       V14_output_0, V14_output_1, V14_output_2, V15_output_0, V15_output_1, V15_output_2;

  double_demux WriteEnableController (
    .Select1(WriteToResgisterX), .Select2(WriteToResgisterX), .Input1(EnableWrite1), .Input2(EnableWrite1),
    .Output0(WriteEnableController_output0), .Output1(WriteEnableController_output1),
    .Output9(WriteEnableController_output9), .Output10(WriteEnableController_output10),
    .output11(WriteEnableController_output11), .Output12(WriteEnableController_output12),
    .Output13(WriteEnableController_output13), .Output2(WriteEnableController_output2),
    .Output3(WriteEnableController_output3), .Output4(WriteEnableController_output4),
    .Output5(WriteEnableController_output5), .Output6(WriteEnableController_output6),
    .Output7(WriteEnableController_output7), .OUtput8(WriteEnableController_output8),
    .Output14(WriteEnableController_output14), .Output15(WriteEnableController_output15));
  double_demux ReadEnableController (
    .Select1(ClearRegisterX), .Select2(ClearRegisterY), .Input1(ClearEnableX), .Input2(ClearEnableY),
    .Output0(ReadEnableController_output0), .Output1(ReadEnableController_output1),
    .Output9(ReadEnableController_output9), .Output10(ReadEnableController_output10),
    .output11(ReadEnableController_output11), .Output12(ReadEnableController_output12),
    .Output13(ReadEnableController_output13), .Output2(ReadEnableController_output2),
    .Output3(ReadEnableController_output3), .Output4(ReadEnableController_output4),
    .Output5(ReadEnableController_output5), .Output6(ReadEnableController_output6),
    .Output7(ReadEnableController_output7), .OUtput8(ReadEnableController_output8),
    .Output14(ReadEnableController_output14), .Output15(ReadEnableController_output15));
  vector_register V0 (
    .Clock(Clock), .WriteEnable(WriteEnableController_output0), .Clear(ReadEnableController_output0),
    .Input_0(inputA0), .Input_1(inputA1), .Input_2(inputA2), .Output_0(V0_output_0), .Output_1(V0_output_1),
    .Output_2(V0_output_2));
  vector_register V8 (
    .Clock(Clock), .WriteEnable(WriteEnableController_output8), .Clear(ReadEnableController_output8),
    .Input_0(inputA0), .Input_1(inputA1), .Input_2(inputA2), .Output_0(V8_output_0), .Output_1(V8_output_1),
    .Output_2(V8_output_2));
  vector_register V9 (
    .Clock(Clock), .WriteEnable(WriteEnableController_output9), .Clear(ReadEnableController_output9),
    .Input_0(inputA0), .Input_1(inputA1), .Input_2(inputA2), .Output_0(V9_output_0), .Output_1(V9_output_1),
    .Output_2(V9_output_2));
  vector_register V1 (
    .Clock(Clock), .WriteEnable(WriteEnableController_output1), .Clear(ReadEnableController_output1),
    .Input_0(inputA0), .Input_1(inputA1), .Input_2(inputA2), .Output_0(V1_output_0), .Output_1(V1_output_1),
    .Output_2(V1_output_2));
  vector_register V10 (
    .Clock(Clock), .WriteEnable(WriteEnableController_output10), .Clear(ReadEnableController_output10),
    .Input_0(inputA0), .Input_1(inputA1), .Input_2(inputA2), .Output_0(V10_output_0),
    .Output_1(V10_output_1), .Output_2(V10_output_2));
  vector_register V2 (
    .Clock(Clock), .WriteEnable(WriteEnableController_output2), .Clear(ReadEnableController_output2),
    .Input_0(inputA0), .Input_1(inputA1), .Input_2(inputA2), .Output_0(V2_output_0), .Output_1(V2_output_1),
    .Output_2(V2_output_2));
  vector_register V11 (
    .Clock(Clock), .WriteEnable(WriteEnableController_output11), .Clear(ReadEnableController_output11),
    .Input_0(inputA0), .Input_1(inputA1), .Input_2(inputA2), .Output_0(V11_output_0),
    .Output_1(V11_output_1), .Output_2(V11_output_2));
  vector_register V3 (
    .Clock(Clock), .WriteEnable(WriteEnableController_output3), .Clear(ReadEnableController_output3),
    .Input_0(inputA0), .Input_1(inputA1), .Input_2(inputA2), .Output_0(V3_output_0), .Output_1(V3_output_1),
    .Output_2(V3_output_2));
  vector_register V12 (
    .Clock(Clock), .WriteEnable(WriteEnableController_output12), .Clear(ReadEnableController_output12),
    .Input_0(inputA0), .Input_1(inputA1), .Input_2(inputA2), .Output_0(V12_output_0),
    .Output_1(V12_output_1), .Output_2(V12_output_2));
  vector_register V4 (
    .Clock(Clock), .WriteEnable(WriteEnableController_output4), .Clear(ReadEnableController_output4),
    .Input_0(inputA0), .Input_1(inputA1), .Input_2(inputA2), .Output_0(V4_output_0), .Output_1(V4_output_1),
    .Output_2(V4_output_2));
  vector_register V5 (
    .Clock(Clock), .WriteEnable(WriteEnableController_output5), .Clear(ReadEnableController_output5),
    .Input_0(inputA0), .Input_1(inputA1), .Input_2(inputA2), .Output_0(V5_output_0), .Output_1(V5_output_1),
    .Output_2(V5_output_2));
  vector_register V13 (
    .Clock(Clock), .WriteEnable(WriteEnableController_output13), .Clear(ReadEnableController_output13),
    .Input_0(inputA0), .Input_1(inputA1), .Input_2(inputA2), .Output_0(V13_output_0),
    .Output_1(V13_output_1), .Output_2(V13_output_2));
  vector_register V6 (
    .Clock(Clock), .WriteEnable(WriteEnableController_output6), .Clear(ReadEnableController_output6),
    .Input_0(inputA0), .Input_1(inputA1), .Input_2(inputA2), .Output_0(V6_output_0), .Output_1(V6_output_1),
    .Output_2(V6_output_2));
  vector_register V14 (
    .Clock(Clock), .WriteEnable(WriteEnableController_output14), .Clear(ReadEnableController_output14),
    .Input_0(inputA0), .Input_1(inputA1), .Input_2(inputA2), .Output_0(V14_output_0),
    .Output_1(V14_output_1), .Output_2(V14_output_2));
  vector_register V7 (
    .Clock(Clock), .WriteEnable(WriteEnableController_output7), .Clear(ReadEnableController_output7),
    .Input_0(inputA0), .Input_1(inputA1), .Input_2(inputA2), .Output_0(V7_output_0), .Output_1(V7_output_1),
    .Output_2(V7_output_2));
  vector_register V15 (
    .Clock(Clock), .WriteEnable(WriteEnableController_output15), .Clear(ReadEnableController_output15),
    .Input_0(inputA0), .Input_1(inputA1), .Input_2(inputA2), .Output_0(V15_output_0),
    .Output_1(V15_output_1), .Output_2(V15_output_2));
  vector_mux vector_mux_1 (
    .input61(V6_output_1), .input62(V6_output_2), .input00(V0_output_0), .input70(V7_output_0),
    .input71(V7_output_1), .input72(V7_output_2), .input80(V8_output_0), .input81(V8_output_1),
    .input82(V8_output_2), .input90(V9_output_0), .input91(V9_output_1), .input92(V9_output_2),
    .input01(V0_output_1), .input100(V10_output_0), .input101(V10_output_1), .input102(V10_output_2),
    .input110(V11_output_0), .input111(V11_output_1), .input112(V11_output_2), .input120(V12_output_0),
    .input121(V12_output_1), .input02(V0_output_2), .input122(V12_output_2), .input130(V13_output_0),
    .input131(V13_output_1), .input132(V13_output_2), .input140(V14_output_0), .input141(V14_output_1),
    .input142(V14_output_2), .input150(V15_output_0), .input151(V15_output_1), .input152(V15_output_2),
    .input10(V1_output_0), .input11(V1_output_1), .input12(V1_output_2), .input20(V2_output_0),
    .input21(V2_output_1), .input22(V2_output_2), .input30(V3_output_0), .input31(V3_output_1),
    .input32(V3_output_2), .input40(V4_output_0), .input41(V4_output_1), .input42(V4_output_2),
    .input50(V5_output_0), .input51(V5_output_1), .input52(V5_output_2), .input60(V6_output_0),
    .selectBits(RegisterToReadX), .Output0(X0), .Output1(X1), .Output2(X2));
  vector_mux vector_mux_2 (
    .input61(V6_output_1), .input62(V6_output_2), .input00(V0_output_0), .input70(V7_output_0),
    .input71(V7_output_1), .input72(V7_output_2), .input80(V8_output_0), .input81(V8_output_1),
    .input82(V8_output_2), .input90(V9_output_0), .input91(V9_output_1), .input92(V9_output_2),
    .input01(V0_output_1), .input100(V10_output_0), .input101(V10_output_1), .input102(V10_output_2),
    .input110(V11_output_0), .input111(V11_output_1), .input112(V11_output_2), .input120(V12_output_0),
    .input121(V12_output_1), .input02(V0_output_2), .input122(V12_output_2), .input130(V13_output_0),
    .input131(V13_output_1), .input132(V13_output_2), .input140(V14_output_0), .input141(V14_output_1),
    .input142(V14_output_2), .input150(V15_output_0), .input151(V15_output_1), .input152(V15_output_2),
    .input10(V1_output_0), .input11(V1_output_1), .input12(V1_output_2), .input20(V2_output_0),
    .input21(V2_output_1), .input22(V2_output_2), .input30(V3_output_0), .input31(V3_output_1),
    .input32(V3_output_2), .input40(V4_output_0), .input41(V4_output_1), .input42(V4_output_2),
    .input50(V5_output_0), .input51(V5_output_1), .input52(V5_output_2), .input60(V6_output_0),
    .selectBits(RegisterToReadY), .Output0(Y0), .Output1(Y2), .Output2(Y3));
endmodule

module vector_register (
  input  WriteEnable,
  input  [31:0] Input_0,
  input  Clock,
  input  [31:0] Input_1,
  input  [31:0] Input_2,
  input  Clear,
  output [31:0] Output_0,
  output [31:0] Output_1,
  output [31:0] Output_2
);

  Register #(.width(32)) v_sub_0 (.D(Input_0), .en(WriteEnable), .clk(Clock), .Q(Output_0), .clr(Clear));
  Register #(.width(32)) v_sub_1 (.D(Input_1), .en(WriteEnable), .clk(Clock), .Q(Output_1), .clr(Clear));
  Register #(.width(32)) v_sub_2 (.D(Input_2), .en(WriteEnable), .clk(Clock), .Q(Output_2));  // open: clr
endmodule

module double_demux (
  input  [3:0] Select1,
  input  [3:0] Select2,
  input  Input2,
  input  Input1,
  output Output0,
  output Output1,
  output Output2,
  output Output3,
  output Output4,
  output Output5,
  output Output6,
  output Output7,
  output OUtput8,
  output Output9,
  output Output10,
  output output11,
  output Output12,
  output Output13,
  output Output14,
  output Output15
);

  wire demultiplexer_1_out0, demultiplexer_1_out1, demultiplexer_1_out2, demultiplexer_1_out3,
       demultiplexer_1_out4, demultiplexer_1_out5, demultiplexer_1_out6, demultiplexer_1_out7,
       demultiplexer_1_out8, demultiplexer_1_out9, demultiplexer_1_out10, demultiplexer_1_out11,
       demultiplexer_1_out12, demultiplexer_1_out13, demultiplexer_1_out14, demultiplexer_1_out15,
       demultiplexer_2_out0, demultiplexer_2_out1, demultiplexer_2_out2, demultiplexer_2_out3,
       demultiplexer_2_out4, demultiplexer_2_out5, demultiplexer_2_out6, demultiplexer_2_out7,
       demultiplexer_2_out8, demultiplexer_2_out9, demultiplexer_2_out10, demultiplexer_2_out11,
       demultiplexer_2_out12, demultiplexer_2_out13, demultiplexer_2_out14, demultiplexer_2_out15;

  Demultiplexer #(.select(4)) demultiplexer_1 (
    .out0(demultiplexer_1_out0), .out1(demultiplexer_1_out1), .out2(demultiplexer_1_out2),
    .out3(demultiplexer_1_out3), .out4(demultiplexer_1_out4), .out5(demultiplexer_1_out5),
    .out6(demultiplexer_1_out6), .out7(demultiplexer_1_out7), .out8(demultiplexer_1_out8),
    .out9(demultiplexer_1_out9), .out10(demultiplexer_1_out10), .out11(demultiplexer_1_out11),
    .out12(demultiplexer_1_out12), .out13(demultiplexer_1_out13), .out14(demultiplexer_1_out14),
    .out15(demultiplexer_1_out15), .in(Input1), .sel(Select1));
  Demultiplexer #(.select(4)) demultiplexer_2 (
    .out0(demultiplexer_2_out0), .out1(demultiplexer_2_out1), .out2(demultiplexer_2_out2),
    .out3(demultiplexer_2_out3), .out4(demultiplexer_2_out4), .out5(demultiplexer_2_out5),
    .out6(demultiplexer_2_out6), .out7(demultiplexer_2_out7), .out8(demultiplexer_2_out8),
    .out9(demultiplexer_2_out9), .out10(demultiplexer_2_out10), .out11(demultiplexer_2_out11),
    .out12(demultiplexer_2_out12), .out13(demultiplexer_2_out13), .out14(demultiplexer_2_out14),
    .out15(demultiplexer_2_out15), .in(Input2), .sel(Select2));
  or or_1 (Output0, demultiplexer_1_out0, demultiplexer_2_out0);
  or or_2 (Output1, demultiplexer_1_out1, demultiplexer_2_out1);
  or or_3 (Output2, demultiplexer_1_out2, demultiplexer_2_out2);
  or or_4 (Output3, demultiplexer_1_out3, demultiplexer_2_out3);
  or or_5 (Output4, demultiplexer_1_out4, demultiplexer_2_out4);
  or or_6 (Output5, demultiplexer_1_out5, demultiplexer_2_out5);
  or or_7 (Output6, demultiplexer_1_out6, demultiplexer_2_out6);
  or or_8 (Output7, demultiplexer_1_out7, demultiplexer_2_out7);
  or or_9 (OUtput8, demultiplexer_1_out8, demultiplexer_2_out8);
  or or_10 (Output9, demultiplexer_1_out9, demultiplexer_2_out9);
  or or_11 (Output10, demultiplexer_1_out10, demultiplexer_2_out10);
  or or_12 (output11, demultiplexer_1_out11, demultiplexer_2_out11);
  or or_13 (Output12, demultiplexer_1_out12, demultiplexer_2_out12);
  or or_14 (Output13, demultiplexer_1_out13, demultiplexer_2_out13);
  or or_15 (Output14, demultiplexer_1_out14, demultiplexer_2_out14);
  or or_16 (Output15, demultiplexer_1_out15, demultiplexer_2_out15);
endmodule

module vector_mux (
  input  [31:0] input00,
  input  [31:0] input01,
  input  [31:0] input02,
  input  [31:0] input10,
  input  [31:0] input11,
  input  [31:0] input12,
  input  [31:0] input20,
  input  [31:0] input21,
  input  [31:0] input22,
  input  [31:0] input30,
  input  [31:0] input31,
  input  [31:0] input32,
  input  [31:0] input40,
  input  [31:0] input41,
  input  [31:0] input42,
  input  [31:0] input50,
  input  [31:0] input51,
  input  [31:0] input52,
  input  [31:0] input60,
  input  [31:0] input61,
  input  [31:0] input62,
  input  [31:0] input70,
  input  [31:0] input71,
  input  [31:0] input72,
  input  [31:0] input80,
  input  [31:0] input81,
  input  [31:0] input82,
  input  [31:0] input90,
  input  [31:0] input91,
  input  [31:0] input92,
  input  [31:0] input100,
  input  [31:0] input101,
  input  [31:0] input102,
  input  [31:0] input110,
  input  [31:0] input111,
  input  [31:0] input112,
  input  [31:0] input120,
  input  [31:0] input121,
  input  [31:0] input122,
  input  [31:0] input130,
  input  [31:0] input131,
  input  [31:0] input132,
  input  [31:0] input140,
  input  [31:0] input141,
  input  [31:0] input142,
  input  [31:0] input150,
  input  [31:0] input151,
  input  [31:0] input152,
  input  [3:0] selectBits,
  output [31:0] Output0,
  output [31:0] Output1,
  output [31:0] Output2
);

  Multiplexer #(.select(4), .width(32)) multiplexer_1 (
    .in0(input00), .in1(input10), .in2(input20), .in3(input30), .in4(input40), .in5(input50), .in6(input60),
    .in7(input70), .in8(input80), .in9(input90), .in10(input100), .in11(input110), .in12(input120),
    .in13(input130), .in14(input140), .in15(input150), .out(Output0), .sel(selectBits));
  Multiplexer #(.select(4), .width(32)) multiplexer_2 (
    .in0(input01), .in1(input11), .in2(input21), .in3(input31), .in4(input41), .in5(input51), .in6(input61),
    .in7(input71), .in8(input81), .in9(input91), .in10(input101), .in11(input111), .in12(input121),
    .in13(input131), .in14(input141), .in15(input151), .out(Output1), .sel(selectBits));
  Multiplexer #(.select(4), .width(32)) multiplexer_3 (
    .in0(input02), .in1(input12), .in2(input22), .in3(input32), .in4(input42), .in5(input52), .in6(input62),
    .in7(input72), .in8(input82), .in9(input92), .in10(input102), .in11(input112), .in12(input122),
    .in13(input132), .in14(input142), .in15(input152), .out(Output2), .sel(selectBits));
endmodule

module Instruction (
  input  [31:0] Instruction,
  input  [2:0] in_2,
  input  [6:0] Funct7,
  input  [2:0] Funct3,
  output [6:0] out_5,
  output [2:0] out_6,
  output [4:0] out_7,
  output [4:0] out_8,
  output [31:0] out_9,
  output out_10,
  output out_11,
  output out_12,
  output out_13,
  output IsIntFunct7,
  output out_15,
  output out_16,
  output out_17,
  output out_18
);

  wire and_9_out, and_10_out, and_11_out, and_12_out, and_13_out, multiplexer_2_out;
  wire [2:0] int_decoder_1_funct3, int_funct7_reducer_1_reduce;
  wire [6:0] int_decoder_1_funct7;
  wire [31:0] multiplexer_1_out;

  int_type_idetifier int_type_idetifier_1 (.Opcode(out_5), .InType(out_6));
  and and_1 (out_10, ~Funct3[0], ~Funct3[1], ~Funct3[2]);  // AND_Gate
  and and_2 (out_11, Funct3[0], ~Funct3[1], ~Funct3[2]);  // AND_Gate
  and and_3 (out_12, ~Funct3[0], Funct3[1], ~Funct3[2]);  // AND_Gate
  and and_4 (out_13, Funct3[0], Funct3[1], ~Funct3[2]);  // AND_Gate
  and and_5 (out_15, ~Funct3[0], ~Funct3[1], Funct3[2]);  // AND_Gate
  and and_6 (out_16, Funct3[0], ~Funct3[1], Funct3[2]);  // AND_Gate
  and and_7 (out_17, ~Funct3[0], Funct3[1], Funct3[2]);  // AND_Gate
  and and_8 (out_18, Funct3[0], Funct3[1], Funct3[2]);
  int_decoder int_decoder_1 (
    .Instruction(Instruction), .InType(out_6), .Opcode(out_5), .RD(out_7), .Funct3(int_decoder_1_funct3),
    .RS2(out_8), .Funct7(int_decoder_1_funct7), .Imm(out_9));  // open: RS1
  int_funct7_reducer int_funct7_reducer_1 (.Funct7(int_decoder_1_funct7), .Reduce(int_funct7_reducer_1_reduce));
  ALUINT aluint_1 (
    .Func3(int_decoder_1_funct3), .Func7Red(int_funct7_reducer_1_reduce), .op2(multiplexer_1_out));  // open: op1
  Multiplexer #(.width(32)) multiplexer_1 (.in1(out_9), .out(multiplexer_1_out));  // open: in0, sel
  and and_9 (and_9_out, ~Funct7[0], ~Funct7[1], ~Funct7[2], ~Funct7[3], ~Funct7[4], ~Funct7[5], ~Funct7[6]);  // AND_Gate
  and and_10 (and_10_out, ~Funct7[0], ~Funct7[1], ~Funct7[2], ~Funct7[3], ~Funct7[4], Funct7[5], ~Funct7[6]);  // AND_Gate
  and and_11 (and_11_out, Funct7[0], ~Funct7[1], ~Funct7[2], ~Funct7[3], ~Funct7[4], ~Funct7[5], ~Funct7[6]);  // AND_Gate
  and and_12 (and_12_out, ~Funct7[0], ~Funct7[1], ~Funct7[2], Funct7[3], ~Funct7[4], ~Funct7[5], ~Funct7[6]);  // AND_Gate
  and and_13 (and_13_out, ~Funct7[0], ~Funct7[1], ~Funct7[2], Funct7[3], Funct7[4], ~Funct7[5], ~Funct7[6]);  // AND_Gate
  or or_1 (IsIntFunct7, and_9_out, and_10_out, and_11_out, and_12_out, and_13_out);
  Multiplexer #(.select(3)) multiplexer_2 (
    .out(multiplexer_2_out), .sel(in_2));  // open: in0, in1, in2, in3, in4, in5, in6, in7

  // Notes on the sheet:
  //   JALR - BEQ - LB - SB - ADDI - ADD - SUB-  FENCE - ECALL - EBREAK - MUL
  //   BNE - LH - SH -SLLI - SLL - MULH
  //   LW - SW - SLTI - SLT - MULHSU
  //   SLTIU - SLTU - MULHU
  //   BLT - LBU - XORI - XOR - DIV
  //   BGE - LHU - SRLI - SRAI - SRL -SRA - DIVU
  //   BLTU - ORI - OR - REM
  //   BGEU - ANDI - AND - REMU
  //   Pueden unirse en 1 de 7 bits con el primer bit para indicar activar ALU.
  //   SRAI - SUB -SRA
  //   MUL - MULH - MULHSU - MULHSU - MULHU - DIV - DIVU - REM - REMU
  //   SRET - WFI
  //   MRET
  //   SLLI - SRLI - ADD - SLL - SLT - SLTU - XOR - SRL - OR - AND
endmodule

module int_decoder (
  input  [31:0] Instruction,
  input  [2:0] InType,
  output [6:0] Opcode,
  output [4:0] RD,
  output [2:0] Funct3,
  output [4:0] RS1,
  output [4:0] RS2,
  output [6:0] Funct7,
  output [31:0] Imm
);

  wire [10:0] bit_extender_4_out;
  wire [18:0] bit_extender_3_out;
  wire [19:0] bit_extender_1_out, bit_extender_2_out;

  assign bit_extender_1_out = {{19{Instruction[31]}}, Instruction[31]};  // Bit_Extender bit_extender_1
  assign bit_extender_2_out = {{19{Instruction[31]}}, Instruction[31]};  // Bit_Extender bit_extender_2
  assign bit_extender_3_out = {{18{Instruction[31]}}, Instruction[31]};  // Bit_Extender bit_extender_3
  assign bit_extender_4_out = {{10{Instruction[31]}}, Instruction[31]};  // Bit_Extender bit_extender_4
  Multiplexer #(.select(3), .width(32)) multiplexer_1 (
    .in1({bit_extender_1_out, Instruction[31:20]}),
    .in2({bit_extender_2_out, Instruction[31:25], Instruction[11:7]}),
    .in3({bit_extender_3_out, Instruction[31], Instruction[7], Instruction[30:25], Instruction[11:8], 1'b0}),
    .in4({Instruction[31:12], {12{1'b0}}}),
    .in5({bit_extender_4_out, Instruction[31], Instruction[19:12], Instruction[20], Instruction[30:21], 1'b0}),
    .in6({32{1'b0}}), .in7({32{1'b0}}), .out(Imm), .sel(InType));  // open: in0

  assign Funct3 = Instruction[14:12];
  assign Funct7 = Instruction[31:25];
  assign Opcode = Instruction[6:0];
  assign RD = Instruction[11:7];
  assign RS1 = Instruction[19:15];
  assign RS2 = Instruction[24:20];

  // Notes on the sheet:
  //   R-Type
  //   I-Type
  //   S-Type
  //   B-Type
  //   U-Type
  //   J-Type
  //   001
  //   010
  //   011
  //   100
  //   101
endmodule

module int_opcode_identifier (
  input  [6:0] Opcode,
  output LUI,
  output AUIPC,
  output JAL,
  output JALR,
  output BRANCH,
  output LOAD,
  output STORE,
  output ALI,
  output ALR,
  output FENCE,
  output ECB
);

  and and_1 (LUI, Opcode[0], Opcode[1], Opcode[2], ~Opcode[3], Opcode[4], Opcode[5], ~Opcode[6]);  // AND_Gate
  and and_2 (AUIPC, Opcode[0], Opcode[1], Opcode[2], ~Opcode[3], Opcode[4], ~Opcode[5], ~Opcode[6]);  // AND_Gate
  and and_3 (JAL, Opcode[0], Opcode[1], Opcode[2], Opcode[3], ~Opcode[4], Opcode[5], Opcode[6]);  // AND_Gate
  and and_4 (JALR, Opcode[0], Opcode[1], Opcode[2], ~Opcode[3], ~Opcode[4], Opcode[5], Opcode[6]);  // AND_Gate
  and and_5 (BRANCH, Opcode[0], Opcode[1], ~Opcode[2], ~Opcode[3], ~Opcode[4], Opcode[5], Opcode[6]);  // AND_Gate
  and and_6 (LOAD, Opcode[0], Opcode[1], ~Opcode[2], ~Opcode[3], ~Opcode[4], ~Opcode[5], ~Opcode[6]);  // AND_Gate
  and and_7 (STORE, Opcode[0], Opcode[1], ~Opcode[2], ~Opcode[3], ~Opcode[4], Opcode[5], ~Opcode[6]);  // AND_Gate
  and and_8 (ALI, Opcode[0], Opcode[1], ~Opcode[2], ~Opcode[3], Opcode[4], ~Opcode[5], ~Opcode[6]);  // AND_Gate
  and and_9 (ALR, Opcode[0], Opcode[1], ~Opcode[2], ~Opcode[3], Opcode[4], Opcode[5], ~Opcode[6]);  // AND_Gate
  and and_10 (FENCE, Opcode[0], Opcode[1], Opcode[2], Opcode[3], ~Opcode[4], ~Opcode[5], ~Opcode[6]);  // AND_Gate
  and and_11 (ECB, Opcode[0], Opcode[1], ~Opcode[2], ~Opcode[3], Opcode[4], Opcode[5], Opcode[6]);  // AND_Gate

  // Notes on the sheet:
  //   Arithmetic-Logic operations with register
  //   Arithmetic-Logic operation with Immediate
  //   I
  //   S
  //   I
  //   R
endmodule

module int_funct3_identifier (
  input  [2:0] Funct3,
  output out_2,
  output out_3,
  output out_4,
  output out_5,
  output out_6,
  output out_7,
  output out_8,
  output out_9
);

  and and_1 (out_2, ~Funct3[0], ~Funct3[1], ~Funct3[2]);  // AND_Gate
  and and_2 (out_3, Funct3[0], ~Funct3[1], ~Funct3[2]);  // AND_Gate
  and and_3 (out_4, ~Funct3[0], Funct3[1], ~Funct3[2]);  // AND_Gate
  and and_4 (out_5, Funct3[0], Funct3[1], ~Funct3[2]);  // AND_Gate
  and and_5 (out_6, ~Funct3[0], ~Funct3[1], Funct3[2]);  // AND_Gate
  and and_6 (out_7, Funct3[0], ~Funct3[1], Funct3[2]);  // AND_Gate
  and and_7 (out_8, ~Funct3[0], Funct3[1], Funct3[2]);  // AND_Gate
  and and_8 (out_9, Funct3[0], Funct3[1], Funct3[2]);

  // Notes on the sheet:
  //   JALR - BEQ - LB - SB - ADDI - ADD - SUB-  FENCE - ECALL - EBREAK - MUL
  //   BNE - LH - SH -SLLI - SLL - MULH
  //   LW - SW - SLTI - SLT - MULHSU
  //   SLTIU - SLTU - MULHU
  //   BLT - LBU - XORI - XOR - DIV
  //   BGE - LHU - SRLI - SRAI - SRL -SRA - DIVU
  //   BLTU - ORI - OR - REM
  //   BGEU - ANDI - AND - REMU
endmodule

module int_funct7_reducer (
  input  [6:0] Funct7,
  output [2:0] Reduce
);

  wire and_1_out, and_2_out, and_3_out, and_4_out, and_5_out;

  and and_1 (and_1_out, ~Funct7[0], ~Funct7[1], ~Funct7[2], ~Funct7[3], ~Funct7[4], ~Funct7[5], ~Funct7[6]);  // AND_Gate
  and and_2 (and_2_out, ~Funct7[0], ~Funct7[1], ~Funct7[2], ~Funct7[3], ~Funct7[4], Funct7[5], ~Funct7[6]);  // AND_Gate
  and and_3 (and_3_out, Funct7[0], ~Funct7[1], ~Funct7[2], ~Funct7[3], ~Funct7[4], ~Funct7[5], ~Funct7[6]);  // AND_Gate
  and and_4 (and_4_out, ~Funct7[0], ~Funct7[1], ~Funct7[2], Funct7[3], ~Funct7[4], ~Funct7[5], ~Funct7[6]);  // AND_Gate
  and and_5 (and_5_out, ~Funct7[0], ~Funct7[1], ~Funct7[2], Funct7[3], Funct7[4], ~Funct7[5], ~Funct7[6]);  // AND_Gate
  Priority_Encoder priority_encoder_1 (
    .in0(and_1_out), .in1(and_2_out), .in2(and_3_out), .in3(and_4_out), .in4(and_5_out), .in5(1'b0),
    .in6(1'b0), .in7(1'b0), .out(Reduce));  // open: en_in, gs, en_out

  // Notes on the sheet:
  //   SRAI - SUB -SRA
  //   MUL - MULH - MULHSU - MULHSU - MULHU - DIV - DIVU - REM - REMU
  //   SRET - WFI
  //   MRET
  //   SLLI - SRLI - ADD - SLL - SLT - SLTU - XOR - SRL - OR - AND
endmodule

module ALUINT (
  input  [2:0] Func3,
  input  [2:0] Func7Red,
  input  [31:0] op1,
  input  [31:0] op2
);

  wire multiplexer_1_out, multiplexer_2_out;

  Multiplexer #(.select(3)) multiplexer_1 (
    .out(multiplexer_1_out), .sel(Func3));  // open: in0, in1, in2, in3, in4, in5, in6, in7
  Multiplexer #(.select(3)) multiplexer_2 (
    .out(multiplexer_2_out), .sel(Func7Red));  // open: in0, in1, in2, in3, in4, in5, in6, in7
endmodule

module int_type_idetifier (
  input  [6:0] Opcode,
  output [2:0] InType
);

  wire and_1_out, and_2_out, and_3_out, and_4_out, and_5_out, and_6_out, and_7_out, and_8_out, and_9_out,
       and_10_out, or_1_out, or_2_out;

  and and_1 (and_1_out, Opcode[0], Opcode[1], ~Opcode[2], ~Opcode[3], Opcode[4], Opcode[5], ~Opcode[6]);  // AND_Gate
  and and_2 (and_2_out, Opcode[0], Opcode[1], ~Opcode[2], ~Opcode[3], ~Opcode[4], ~Opcode[5], ~Opcode[6]);  // AND_Gate
  and and_3 (and_3_out, Opcode[0], Opcode[1], Opcode[2], ~Opcode[3], ~Opcode[4], Opcode[5], Opcode[6]);  // AND_Gate
  and and_4 (and_4_out, Opcode[0], Opcode[1], ~Opcode[2], ~Opcode[3], Opcode[4], ~Opcode[5], ~Opcode[6]);  // AND_Gate
  and and_5 (and_5_out, Opcode[0], Opcode[1], ~Opcode[2], ~Opcode[3], Opcode[4], Opcode[5], Opcode[6]);  // AND_Gate
  and and_6 (and_6_out, Opcode[0], Opcode[1], ~Opcode[2], ~Opcode[3], ~Opcode[4], Opcode[5], ~Opcode[6]);  // AND_Gate
  and and_7 (and_7_out, Opcode[0], Opcode[1], ~Opcode[2], ~Opcode[3], ~Opcode[4], Opcode[5], Opcode[6]);  // AND_Gate
  and and_8 (and_8_out, Opcode[0], Opcode[1], Opcode[2], ~Opcode[3], Opcode[4], Opcode[5], ~Opcode[6]);  // AND_Gate
  and and_9 (and_9_out, Opcode[0], Opcode[1], Opcode[2], ~Opcode[3], Opcode[4], ~Opcode[5], ~Opcode[6]);  // AND_Gate
  and and_10 (and_10_out, Opcode[0], Opcode[1], Opcode[2], Opcode[3], ~Opcode[4], Opcode[5], Opcode[6]);  // AND_Gate
  or or_1 (or_1_out, and_2_out, and_3_out, and_4_out, and_5_out);
  or or_2 (or_2_out, and_8_out, and_9_out);
  Priority_Encoder priority_encoder_1 (
    .in0(and_1_out), .in1(or_1_out), .in2(and_6_out), .in3(and_7_out), .in4(or_2_out), .in5(and_10_out),
    .in6(1'b0), .in7(1'b0), .out(InType));  // open: en_in, gs, en_out

  // Notes on the sheet:
  //   RType
  //   IType
  //   SType
  //   BType
  //   UType
  //   JType
endmodule

// VHDL entity float_opcode_identifier, as the project stores it:
--------------------------------------------------------------------------------
-- Project :
-- File    :
-- Autor   :
-- Date    :
--
--------------------------------------------------------------------------------
-- Description :
--
--------------------------------------------------------------------------------

LIBRARY ieee;
USE ieee.std_logic_1164.ALL;

ENTITY float_opcode_identifier IS
    PORT (
        -- Input ports
        b1, b2, b3, b4, b5, b6, b7 : IN STD_LOGIC;
        -- Output ports
        is_valid : OUT STD_LOGIC
    );
END float_opcode_identifier;

--------------------------------------------------------------------------------
--Complete your VHDL description below
--------------------------------------------------------------------------------

ARCHITECTURE Identify OF float_opcode_identifier IS

BEGIN

    PROCESS (b1, b2, b3, b4, b5, b6, b7)
    BEGIN
        IF (b1 = '1' AND b2 = '1' AND b3 = '0' AND b4 = '0' AND b5 = '1' AND b6 = '0' AND b7 = '1') 
        OR (b1 = '1' AND b2 = '1' AND b3 = '1' AND b4 = '1' AND b5 = '0' AND b6 = '0' AND b7 = '1') 
        OR (b1 = '1' AND b2 = '1' AND b3 = '1' AND b4 = '0' AND b5 = '0' AND b6 = '0' AND b7 = '1') 
        OR (b1 = '1' AND b2 = '1' AND b3 = '0' AND b4 = '1' AND b5 = '0' AND b6 = '0' AND b7 = '1') 
        OR (b1 = '1' AND b2 = '1' AND b3 = '0' AND b4 = '0' AND b5 = '0' AND b6 = '0' AND b7 = '1') 
        OR (b1 = '1' AND b2 = '1' AND b3 = '1' AND b4 = '0' AND b5 = '0' AND b6 = '1' AND b7 = '0')
        OR (b1 = '1' AND b2 = '1' AND b3 = '1' AND b4 = '0' AND b5 = '0' AND b6 = '0' AND b7 = '0')  
        THEN
            is_valid <= '1';
        ELSE
            is_valid <= '0';
        END IF;
    END PROCESS;
END Identify;
